# Fritzing sketch Schhematic (saved by Fritzing 1.0.3b)
breadboards: 1

parts:
  part = Arduino Uno (Rev3)
  R1 = Resistor [tolerance=±5% power=0.25W resistance=470 package=THT]
  SolarCell = S1133 Si Photodiode [package="8mm Ceramic [THT]"]
  Peristaltic_Pump = DC Motor [voltage_(max)=6V voltage_(min)=3V]
  TP120 = NPN-Transistor [package="TO92 [THT]"]
  Stepper_Motor = Stepper Motor - Bipolar
  StepperMotorController = Pololu A4988 [package=SO16]
  part_2 = Soil Moisture Sensor
  IR_sensor_-_Bottom = fc-51 [package=THT]
  IR_sensor_-_Top = fc-51 [package=THT]
  Main_Switch = Pushbutton [package=THT]
  DS18B20_Temperature_Sensor = TMP36 [part_number=' package=to-92]
  R2 = Resistor [tolerance=±5% power=0.25W resistance=150 package=THT]

nets:
  N1: part.A1, SolarCell.cathode
  N2: part.D10_PWM/SS, StepperMotorController.STEP
  N3: part.D11_PWM/MOSI, StepperMotorController.DIR
  GND: part.GND, SolarCell.anode, TP120.E, StepperMotorController.GND, part_2.GND, IR_sensor_-_Bottom.pin2, IR_sensor_-_Top.pin2, Main_Switch.leg1, DS18B20_Temperature_Sensor.GND
  N4: part.D2, Main_Switch.leg0
  N5: part.D4, R1.Pin_1, DS18B20_Temperature_Sensor.VOUT
  5V: part.5V, R1.Pin_0, StepperMotorController.VDD, IR_sensor_-_Bottom.pin3, IR_sensor_-_Top.pin3, DS18B20_Temperature_Sensor.VCC
  12V: Peristaltic_Pump.pin_1, StepperMotorController.VMOT
  N6: Peristaltic_Pump.pin_2, TP120.C
  N7: TP120.B, R2.Pin_1
  N8: Stepper_Motor.A, StepperMotorController.2B
  N9: Stepper_Motor.C, StepperMotorController.2A
  N10: Stepper_Motor.B, StepperMotorController.1A
  N11: Stepper_Motor.D, StepperMotorController.1B
  N12: StepperMotorController.RESET, StepperMotorController.SLEEP
  D7 - Arduino: part_2.VCC
  A0 - Arduino: part_2.SIG
  A5 - Arduino: IR_sensor_-_Bottom.pin1
  A4 - Arduino: IR_sensor_-_Top.pin1
  A3 Arduino: R2.Pin_0
