# Fritzing sketch MainSCH (saved by Fritzing 1.0.3b)
breadboards: 1

parts:
  Part1 = Arduino Uno (Rev3)
  Temperature_Sensor = TMP36 [package=to-92]
  R1 = Resistor [tolerance=±5% power=0.25W resistance=470 package=THT]
  SolarCell = S1133 Si Photodiode [package="8mm Ceramic [THT]"]
  WaterPump = DC Motor [voltage_(max)=6V voltage_(min)=3V]
  pumpSwithcTR = NPN-Transistor [package="TO92 [THT]"]
  WaterSRLeveler = Stepper Motor - Bipolar
  StepperMController = Pololu A4988 [package=SO16]
  Part2 = Soil Moisture Sensor
  Water_Level_Sensor_Minimum = fc-51 [package=THT]
  Water_Level_Sensor_Maximum = fc-51 [package=THT]

nets:
  N1: Part1.A1, SolarCell.cathode
  N2: Part1.D10_PWM/SS, StepperMController.STEP
  N3: Part1.D11_PWM/MOSI, StepperMController.DIR
  GND: Part1.GND, Temperature_Sensor.GND, SolarCell.anode, pumpSwithcTR.E, StepperMController.GND, Part2.GND, Water_Level_Sensor_Minimum.pin2, Water_Level_Sensor_Maximum.pin2
  N4: Part1.D4, Temperature_Sensor.VOUT, R1.Pin_1
  12V: Part1.VIN, WaterPump.pin_1, StepperMController.VMOT
  5V: Temperature_Sensor.VCC, R1.Pin_0, StepperMController.VDD, Water_Level_Sensor_Minimum.pin3, Water_Level_Sensor_Maximum.pin3
  N5: WaterPump.pin_2, pumpSwithcTR.C
  A3 Arduino: pumpSwithcTR.B
  N6: WaterSRLeveler.A, StepperMController.2B
  N7: WaterSRLeveler.C, StepperMController.2A
  N8: WaterSRLeveler.B, StepperMController.1A
  N9: WaterSRLeveler.D, StepperMController.1B
  N10: StepperMController.RESET, StepperMController.SLEEP
  D7 - Arduino: Part2.VCC
  A0 - Arduino: Part2.SIG
  A5 - Arduino: Water_Level_Sensor_Minimum.pin1
  A4 - Arduino: Water_Level_Sensor_Maximum.pin1
