# Fritzing sketch MainSCH_recovered (saved by Fritzing 1.0.3b)
breadboards: 1

parts:
  Part1 = Arduino Uno (Rev3)
  R1 = Resistor [tolerance=±5% power=0.25W resistance=470 package=THT]
  SolarCell = S1133 Si Photodiode [package="8mm Ceramic [THT]"]
  Peristaltic_Pump = DC Motor [voltage_(max)=6V voltage_(min)=3V]
  TP120 = NPN-Transistor [package="TO92 [THT]"]
  Stepper_Motor = Stepper Motor - Bipolar
  StepperMotorController = Pololu A4988 [package=SO16]
  Part2 = Soil Moisture Sensor
  IR_sensor_-_Bottom = fc-51 [package=THT]
  IR_sensor_-_Top = fc-51 [package=THT]
  Main_Switch = Pushbutton [package=THT]
  DS18B20_Temperature_Sensor = TMP36 [part_number=' package=to-92]
  R2 = Resistor [tolerance=±5% power=0.25W resistance=150 package=THT]

nets:
  N1: Part1.A1, SolarCell.cathode
  N2: Part1.D10_PWM/SS, StepperMotorController.STEP
  N3: Part1.D11_PWM/MOSI, StepperMotorController.DIR
  GND: Part1.GND, SolarCell.anode, TP120.E, StepperMotorController.GND, Part2.GND, IR_sensor_-_Bottom.pin2, IR_sensor_-_Top.pin2, Main_Switch.leg1, DS18B20_Temperature_Sensor.GND
  N4: Part1.D2, Main_Switch.leg0
  N5: Part1.D4, R1.Pin_1, DS18B20_Temperature_Sensor.VOUT
  12V: Part1.VIN, Peristaltic_Pump.pin_1, StepperMotorController.VMOT
  5V: R1.Pin_0, StepperMotorController.VDD, IR_sensor_-_Bottom.pin3, IR_sensor_-_Top.pin3, DS18B20_Temperature_Sensor.VCC
  N6: Peristaltic_Pump.pin_2, TP120.C
  N7: TP120.B, R2.Pin_1
  N8: Stepper_Motor.A, StepperMotorController.2B
  N9: Stepper_Motor.C, StepperMotorController.2A
  N10: Stepper_Motor.B, StepperMotorController.1A
  N11: Stepper_Motor.D, StepperMotorController.1B
  N12: StepperMotorController.RESET, StepperMotorController.SLEEP
  D7 - Arduino: Part2.VCC
  A0 - Arduino: Part2.SIG
  A5 - Arduino: IR_sensor_-_Bottom.pin1
  A4 - Arduino: IR_sensor_-_Top.pin1
  A3 Arduino: R2.Pin_0
